// Logisim project SPRIND.circ as structural Verilog: 9 circuits, main circuit main
module main (
);

  wire Clock_inst_clk, reset_out, step_out, toggle_stepping_out;
  wire [15:0] Alu_inst_result, RegisterFile_inst_src1_out, RegisterFile_inst_src2_out;

  Button toggle_stepping (.out(toggle_stepping_out));
  Button step (.out(step_out));
  Button reset (.out(reset_out));
  ROM #(.addrWidth(10)) ROM_inst ();  // open: addr, data
  SPRIND_Clock Clock_inst (
    .step(step_out), .toggle_stepping(toggle_stepping_out), .rst(reset_out), .clk(Clock_inst_clk));
  SPRIND_Counter Counter_inst (
    .rst(reset_out), .clk(Clock_inst_clk));  // open: displacement, replacement, mode_inc, mode_replace, mode_displace, address
  SPRIND_RegisterFile RegisterFile_inst (
    .clk(Clock_inst_clk), .rst(reset_out), .src2_out(RegisterFile_inst_src2_out),
    .src1_out(RegisterFile_inst_src1_out));  // open: src2_reg_sel, dst_reg_sel, data_in, wr_en, src1_reg_sel
  SPRIND_Alu Alu_inst (
    .input0(RegisterFile_inst_src1_out), .input1(RegisterFile_inst_src2_out), .result(Alu_inst_result));  // open: func, flags_updated, carry, overflow
  SPRIND_TestStack TestStack_inst ();  // open: bit_in, op_push, op_pop, op_and, op_or, op_not, op_overwrite, data_in, en, clk, rst, state, top_of_stack
endmodule

module SPRIND_RegisterFile (
  input  [2:0] src1_reg_sel,
  input  [2:0] src2_reg_sel,
  input  [2:0] dst_reg_sel,
  input  [15:0] data_in,
  input  wr_en,
  input  clk,
  input  rst,
  output [15:0] src1_out,
  output [15:0] src2_out
);

  wire decoder_1_out0, decoder_1_out1, decoder_1_out2, decoder_1_out3, decoder_1_out4, decoder_1_out5,
       decoder_1_out6, decoder_1_out7;
  wire [15:0] a_q, b_q, c_q, sp_q, w_q, x_q, y_q, z_q;

  Decoder #(.select(3)) decoder_1 (
    .out0(decoder_1_out0), .out1(decoder_1_out1), .out2(decoder_1_out2), .out3(decoder_1_out3),
    .out4(decoder_1_out4), .out5(decoder_1_out5), .out6(decoder_1_out6), .out7(decoder_1_out7),
    .sel(dst_reg_sel), .en(wr_en));
  Register #(.width(16)) sp (.D(data_in), .en(decoder_1_out0), .clk(clk), .Q(sp_q), .clr(rst));
  Register #(.width(16)) w (.D(data_in), .en(decoder_1_out1), .clk(clk), .Q(w_q), .clr(rst));
  Register #(.width(16)) x (.D(data_in), .en(decoder_1_out2), .clk(clk), .Q(x_q), .clr(rst));
  Register #(.width(16)) y (.D(data_in), .en(decoder_1_out3), .clk(clk), .Q(y_q), .clr(rst));
  Register #(.width(16)) z (.D(data_in), .en(decoder_1_out4), .clk(clk), .Q(z_q), .clr(rst));
  Register #(.width(16)) a (.D(data_in), .en(decoder_1_out5), .clk(clk), .Q(a_q), .clr(rst));
  Register #(.width(16)) b (.D(data_in), .en(decoder_1_out6), .clk(clk), .Q(b_q), .clr(rst));
  Register #(.width(16)) c (.D(data_in), .en(decoder_1_out7), .clk(clk), .Q(c_q), .clr(rst));
  Multiplexer #(.select(3), .width(16)) multiplexer_1 (
    .in0(sp_q), .in1(w_q), .in2(x_q), .in3(y_q), .in4(z_q), .in5(a_q), .in6(b_q), .in7(c_q), .out(src1_out),
    .sel(src1_reg_sel));
  Multiplexer #(.select(3), .width(16)) multiplexer_2 (
    .in0(sp_q), .in1(w_q), .in2(x_q), .in3(y_q), .in4(z_q), .in5(a_q), .in6(b_q), .in7(c_q), .out(src2_out),
    .sel(src2_reg_sel));
endmodule

module SPRIND_Clock (
  input  step,
  input  toggle_stepping,
  input  rst,
  output clk
);

  wire and_1_out, clock_1_out, d_ff_1_q, j_k_ff_1_q, not_1_out;

  Clock clock_1 (.out(clock_1_out));
  D_Flip_Flop d_ff_1 (.D(toggle_stepping), .clk(clock_1_out), .Q(d_ff_1_q), .reset(rst));  // open: Qn, preset
  and and_1 (and_1_out, toggle_stepping, not_1_out);
  not not_1 (not_1_out, d_ff_1_q);
  J_K_Flip_Flop j_k_ff_1 (
    .J(and_1_out), .K(and_1_out), .clk(clock_1_out), .Q(j_k_ff_1_q), .reset(rst));  // open: Qn, preset
  Multiplexer multiplexer_1 (.in0(clock_1_out), .in1(step), .out(clk), .sel(j_k_ff_1_q));
  LED stepping (.in(j_k_ff_1_q));
endmodule

module SPRIND_Alu (
  input  [3:0] func,
  input  [15:0] input0,
  input  [15:0] input1,
  output [15:0] result,
  output flags_updated,
  output carry,
  output overflow
);

  Adder #(.width(16)) adder_1 (.a(input0), .b(input1), .out(result), .cout(carry));  // open: cin
  CheckOverflow checkoverflow_1 (.input0(input0), .input1(input1), .sum(result), .out_4(overflow));
endmodule

module CheckOverflow (
  input  [15:0] input0,
  input  [15:0] input1,
  input  [15:0] sum,
  output out_4
);

  wire xnor_1_out, xor_1_out;

  xor xor_1 (xor_1_out, input1[15], sum[15]);
  xnor xnor_1 (xnor_1_out, input0[15], input1[15]);
  and and_1 (out_4, xnor_1_out, xor_1_out);
endmodule

module SPRIND_Counter (
  input  rst,
  input  clk,
  input  [14:0] displacement,
  input  [14:0] replacement,
  input  mode_inc,
  input  mode_replace,
  input  mode_displace,
  output [15:0] address
);

  wire or_1_out, or_2_out;
  wire [14:0] adder_1_out, counter_1_q, multiplexer_1_out;

  Adder #(.width(15)) adder_1 (.a(counter_1_q), .b(displacement), .out(adder_1_out));  // open: cin, cout
  Multiplexer #(.width(15)) multiplexer_1 (
    .in0(adder_1_out), .in1(replacement), .out(multiplexer_1_out), .sel(mode_replace));
  or or_1 (or_1_out, mode_inc, mode_replace, mode_displace);
  or or_2 (or_2_out, mode_replace, mode_displace);
  Counter #(.max('h7fff), .width(15)) counter_1 (
    .clr(rst), .load(or_2_out), .up(1'b1), .count(or_1_out), .clk(clk), .D(multiplexer_1_out), .Q(counter_1_q));  // open: carry
  assign address = {{1{1'b0}}, counter_1_q};  // Bit_Extender bit_extender_1
endmodule

module SPRIND_TestStack (
  input  bit_in,
  input  op_push,
  input  op_pop,
  input  op_and,
  input  op_or,
  input  op_not,
  input  op_overwrite,
  input  [15:0] data_in,
  input  en,
  input  clk,
  input  rst,
  output [15:0] state,
  output top_of_stack
);

  wire [15:0] BitStack_for_TestStack_o_state;

  Register #(.width(16)) TS (.D(BitStack_for_TestStack_o_state), .en(en), .clk(clk), .Q(state), .clr(rst));
  SPRIND_BitStack BitStack_for_TestStack (
    .i_state(state), .bit_in(bit_in), .op_push(op_push), .op_pop(op_pop), .op_and(op_and), .op_or(op_or),
    .op_not(op_not), .op_overwrite(op_overwrite), .data_in(data_in), .o_state(BitStack_for_TestStack_o_state));

  assign top_of_stack = state[0];
endmodule

module SPRIND_BitStack (
  input  [15:0] i_state,
  input  bit_in,
  input  op_push,
  input  op_pop,
  input  op_and,
  input  op_or,
  input  op_not,
  input  op_overwrite,
  input  [15:0] data_in,
  output [15:0] o_state
);

  wire and_3_out, not_1_out, or_3_out;
  wire [15:0] and_1_out, and_2_out, bit_extender_1_out, bit_extender_2_out, bit_extender_3_out,
       bit_extender_4_out, multiplexer_1_out, multiplexer_2_out, multiplexer_3_out, multiplexer_4_out,
       multiplexer_5_out, multiplexer_6_out, or_1_out, or_2_out, or_4_out, or_5_out, shifter_1_out,
       shifter_2_out;

  assign bit_extender_1_out = {{15{1'b0}}, bit_in};  // Bit_Extender bit_extender_1
  Multiplexer #(.width(16)) multiplexer_1 (
    .in0({16{1'b0}}), .in1(data_in), .out(multiplexer_1_out), .sel(op_overwrite));
  Shifter #(.width(16)) shifter_1 (.in(i_state), .\dist (4'b0001), .out(shifter_1_out));
  Shifter #(.shift("lr"), .width(16)) shifter_2 (.in(i_state), .\dist (4'b0001), .out(shifter_2_out));
  not not_1 (not_1_out, i_state[0]);
  assign or_1_out = shifter_1_out | bit_extender_1_out;  // OR_Gate or_1, 16 bits wide
  Multiplexer #(.width(16)) multiplexer_2 (
    .in0({16{1'b0}}), .in1(shifter_2_out), .out(multiplexer_2_out), .sel(op_pop));
  assign and_1_out = 16'hfffe & multiplexer_2_out;  // AND_Gate and_1, 16 bits wide
  assign bit_extender_2_out = {{15{1'b0}}, not_1_out};  // Bit_Extender bit_extender_2
  assign and_2_out = i_state & 16'hfffe;  // AND_Gate and_2, 16 bits wide
  Multiplexer #(.width(16)) multiplexer_3 (.in0({16{1'b0}}), .in1(or_1_out), .out(multiplexer_3_out), .sel(op_push));
  Multiplexer #(.width(16)) multiplexer_4 (.in0({16{1'b0}}), .in1(or_2_out), .out(multiplexer_4_out), .sel(op_not));
  assign or_2_out = bit_extender_2_out | and_2_out;  // OR_Gate or_2, 16 bits wide
  and and_3 (and_3_out, i_state[0], i_state[1]);
  or or_3 (or_3_out, i_state[0], i_state[1]);
  assign bit_extender_3_out = {{15{1'b0}}, and_3_out};  // Bit_Extender bit_extender_3
  assign or_4_out = bit_extender_3_out | and_1_out;  // OR_Gate or_4, 16 bits wide
  assign bit_extender_4_out = {{15{1'b0}}, or_3_out};  // Bit_Extender bit_extender_4
  assign or_5_out = bit_extender_4_out | and_1_out;  // OR_Gate or_5, 16 bits wide
  Multiplexer #(.width(16)) multiplexer_5 (.in0({16{1'b0}}), .in1(or_4_out), .out(multiplexer_5_out), .sel(op_and));
  Multiplexer #(.width(16)) multiplexer_6 (.in0({16{1'b0}}), .in1(or_5_out), .out(multiplexer_6_out), .sel(op_or));
  assign o_state = multiplexer_3_out | multiplexer_2_out | multiplexer_5_out | multiplexer_6_out | multiplexer_4_out | multiplexer_1_out;  // OR_Gate or_6, 16 bits wide
endmodule

module SPRIND_InstrDecoder (
  input  [15:0] i_instr,
  output [8:0] o_imm9,
  output [12:0] o_imm13,
  output [7:0] o_imm8,
  output [10:0] o_imm11,
  output [3:0] o_imm4,
  output [2:0] o_imm3,
  output [2:0] o_reg0,
  output [2:0] o_reg1,
  output o_adr_reg_RAI,
  output o_adr_reg_RRA
);


  assign o_adr_reg_RAI = i_instr[3];
  assign o_adr_reg_RRA = i_instr[6];
  assign o_imm3 = i_instr[2:0];
  assign o_imm4 = i_instr[6:3];
  assign o_imm8 = i_instr[10:3];
  assign o_imm9 = i_instr[12:4];
  assign o_imm11 = i_instr[10:0];
  assign o_imm13 = i_instr[12:0];
  assign o_reg0 = i_instr[2:0];
  assign o_reg1 = i_instr[5:3];
endmodule
